# Fritzing sketch 1_arduino (saved by Fritzing 0.9.3b)
breadboards: 1

parts:
  NXP_Precision_9dof1 = Adafruit FXOS8700 + FXAS21002 9 DoF Breakout [part_number="Adafruit #3463"]
  NXP_Precision_9dof2 = Adafruit FXOS8700 + FXAS21002 9 DoF Breakout [part_number="Adafruit #3463"]
  Componente1 = Arduino Nano (Rev3.0)

nets:
  N1: NXP_Precision_9dof1.SDA, NXP_Precision_9dof2.SDA, Componente1.A4
  N2: NXP_Precision_9dof1.SCL, NXP_Precision_9dof2.SCL, Componente1.A5
  GND: NXP_Precision_9dof1.GND, NXP_Precision_9dof2.GND, Componente1.GND
  VIN: NXP_Precision_9dof1.VIN, NXP_Precision_9dof2.VIN, Componente1.VIN

custom parts:
  Adafruit FXOS8700 + FXAS21002 9 DoF Breakout: The NXP Precision 9DoF breakout combines two of the best motion sensors we've tested here at Adafruit: The FXOS8700 3-Axis accelerometer and magnetometer, and the FXAS21002 3-axis gyroscope. These two sensors combine to make a nice 9-DoF kit, that can be used for motion and orientation sensing. In particular, we think this sensor set is ideal for AHRS-based orientation calculations: the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
