# Fritzing sketch system_sketch (saved by Fritzing 0.9.3b)
circuit board: 8.46667cm x 5.64444cm
perfboards: 1

parts:
  NXP_Precision_9dof = Adafruit FXOS8700 + FXAS21002 9 DoF Breakout [part_number="Adafruit #3463"]
  Arduino_Nano_v3_0 = Arduino Nano (Rev3.0)

nets:
  N1: NXP_Precision_9dof.SDA, Arduino_Nano_v3_0.A4
  N2: NXP_Precision_9dof.SCL, Arduino_Nano_v3_0.A5
  GND: NXP_Precision_9dof.GND, Arduino_Nano_v3_0.GND
  VIN: NXP_Precision_9dof.VIN, Arduino_Nano_v3_0.VIN

custom parts:
  Adafruit FXOS8700 + FXAS21002 9 DoF Breakout: The NXP Precision 9DoF breakout combines two of the best motion sensors we've tested here at Adafruit: The FXOS8700 3-Axis accelerometer and magnetometer, and the FXAS21002 3-axis gyroscope. These two sensors combine to make a nice 9-DoF kit, that can be used for motion and orientation sensing. In particular, we think this sensor set is ideal for AHRS-based orientation calculations: the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

// code stored in the sketch: sensor_to_python.ino
#include <Wire.h>
#include <Adafruit_Sensor.h>
#include <Adafruit_FXAS21002C.h>
#include <Adafruit_FXOS8700.h>

Adafruit_FXAS21002C gyro = Adafruit_FXAS21002C(0x0021002C);
Adafruit_FXOS8700 accelmag = Adafruit_FXOS8700(0x8700A, 0x8700B);


// Mag calibration values are calculated via ahrs_calibration.
// These values must be determined for each baord/environment.
// See the image in this sketch folder for the values used
// below.

// Offsets applied to raw x/y/z mag values
float mag_offsets[3]            = { 0.93F, -7.47F, -35.23F };

// Soft iron error compensation matrix
float mag_softiron_matrix[3][3] = { {  0.943,  0.011,  0.020 },
                                    {  0.022,  0.918, -0.008 },
                                    {  0.020, -0.008,  1.156 } };

float mag_field_strength        = 50.23F;

// Offsets applied to compensate for gyro zero-drift error for x/y/z
float gyro_zero_offsets[3]      = { 0.0F, 0.0F, 0.0F };


void setup()
{
  Serial.begin(115200);


  // Initialize the sensors.
  if(!gyro.begin())
  {
    /* There was a problem detecting the gyro ... check your connections */
    Serial.println("Ooops, no gyro detected ... Check your wiring!");
    while(1);
  }

  if(!accelmag.begin(ACCEL_RANGE_4G))
  {
    Serial.println("Ooops, no FXOS8700 detected ... Check your wiring!");
    while(1);
  }

}

void loop(void)
{
  sensors_event_t gyro_event;
  sensors_event_t accel_event;
  sensors_event_t mag_event;

  // Get new data samples
  gyro.getEvent(&gyro_event);
  accelmag.getEvent(&accel_event, &mag_event);


  // Apply mag offset compensation (base values in uTesla)
  float x = mag_event.magnetic.x - mag_offsets[0];
  float y = mag_event.magnetic.y - mag_offsets[1];
  float z = mag_event.magnetic.z - mag_offsets[2];

  // Apply mag soft iron error compensation
  float mx = x * mag_softiron_matrix[0][0] + y * mag_softiron_matrix[0][1] + z * mag_softiron_matrix[0][2];
  float my = x * mag_softiron_matrix[1][0] + y * mag_softiron_matrix[1][1] + z * mag_softiron_matrix[1][2];
  float mz = x * mag_softiron_matrix[2][0] + y * mag_softiron_matrix[2][1] + z * mag_softiron_matrix[2][2];

  // Apply gyro zero-rate error compensation
  float gx = gyro_event.gyro.x + gyro_zero_offsets[0];
  float gy = gyro_event.gyro.y + gyro_zero_offsets[1];
  float gz = gyro_event.gyro.z + gyro_zero_offsets[2];

  // The filter library expects gyro data in degrees/s, but adafruit sensor
  // uses rad/s so we need to convert them first (or adapt the filter lib
  // where they are being converted)
  gx *= 57.2958F;
  gy *= 57.2958F;
  gz *= 57.2958F;
	
	Serial.print("Gyro_X: "); Serial.print(gx); Serial.print("  ");
  Serial.print("Gyro_Y: "); Serial.print(gy); Serial.print("  ");
  Serial.print("Gyro_Z: "); Serial.print(gz); Serial.print("  ");
	Serial.print("Accel_X: "); Serial.print(accel_event.acceleration.x); Serial.print("  ");
  Serial.print("Accel_Y: "); Serial.print(accel_event.acceleration.y); Serial.print("  ");
  Serial.print("Accel_Z: "); Serial.print(accel_event.acceleration.z); Serial.print("  ");
	Serial.print("Mag_X: "); Serial.print(mx); Serial.print("  ");
  Serial.print("Mag_Y: "); Serial.print(my); Serial.print("  ");
  Serial.print("Mag_Z: "); Serial.println(mz);


  delay(10);
}
